# Fritzing sketch sketch (saved by Fritzing 0.9.2b)

parts:
  Raspberry_Pi_Zero1 = Raspberry Pi Zero
  Composant1 = PowerBoost 500 Charger
  Composant2 = Lithium Ion Polymer Battery 3.7v 2500mAh [part_number=328]
  Composant3 = ifusb_l
  BUTTON1 = Waterproof Pushbutton (white)
  LED1 = RGB LED (com. anode, rbg) [package="5 mm [THT]"]
  R2 = Resistor [tolerance=±5% resistance=220 package=THT]
  R3 = Resistor [tolerance=±5% resistance=220 package=THT]
  R4 = Resistor [tolerance=±5% resistance=220 package=THT]
  R5 = Resistor [tolerance=±5% resistance=100k package=THT]
  Q1 = MOSFET-NCHANNEL [package=to-92]
  R6 = Resistor [tolerance=±5% resistance=10k package=THT]
  R7 = Resistor [tolerance=±5% resistance=22k package=THT]
  R8 = Resistor [tolerance=±5% resistance=1k package=THT]
  JP1 = Header 1 [package=1x01_offset]
  JP3 = Header 1 [package=1x01_offset]

nets:
  5V: Raspberry_Pi_Zero1.GPIO2, Raspberry_Pi_Zero1.5V, Composant1.5.0V
  GND: Raspberry_Pi_Zero1.GPIO3, Raspberry_Pi_Zero1.GND, Composant1.GND, Composant2.negative, Composant3.GND, R5.Pin_1, R6.Pin_1, R8.Pin_1
  BUTTON: Raspberry_Pi_Zero1.GPIO19, Composant3.IO0, BUTTON1.no_name_yet#3
  ALIVE: Raspberry_Pi_Zero1.GPIO26, Composant3.SPI_SCK
  SHUTDOWN: Raspberry_Pi_Zero1.GPIO21, Composant3.IO4
  BUT_LED: Raspberry_Pi_Zero1.GPIO12, BUTTON1.no_name_yet#4
  4.2V: Composant1.VBAT, Composant2.positive, Composant3.VCC, R7.Pin_0
  POWER: Composant1.ENABLE, Composant3.IO5, R5.Pin_0
  3.3V: Composant3.3V3, BUTTON1.no_name_yet#1, LED1.common_anode, JP3.1
  N1: Composant3.BOOT0, JP1.1
  BAT_SENSE: Composant3.IO1, Q1.S, R6.Pin_0
  BAT_MONITOR: Composant3.IO2, Q1.G
  R_LED: Composant3.IO3, R2.Pin_0
  B_LED: Composant3.SPI_SDO, R4.Pin_0
  G_LED: Composant3.SPI_SDI, R3.Pin_0
  N2: BUTTON1.no_name_yet#5, R8.Pin_0
  N3: LED1.red_cathode, R2.Pin_1
  N4: LED1.blue_cathode, R4.Pin_1
  N5: LED1.green_cathode, R3.Pin_1
  N6: Q1.D, R7.Pin_1

notes:
  NOTE: remove R13 for pull down
  battery monitor circuit
  always on switch

custom parts:
  Raspberry Pi Zero: The Raspberry Pi Zero is half the size of a Model A+, with twice the utility. A tiny Raspberry Pi that’s affordable enough for any project! · 1Ghz, Single-core CPU · 512MB RAM · Mini HDMI and USB On-The-Go ports · Micro USB power · HAT-compatible 40-pin header
  PowerBoost 500 Charger: The PowerBoost 500C is a little DC/DC boost converter module that can be powered by any 3.7V LiIon/LiPoly battery, and convert the battery output to 5.2V DC for running your 5V projects. At its heart is a TPS61090 boost converter from TI. This boost converter chip has some really nice extras such as low battery detection, 2A internal switch, synchronous conversion, excellent efficiency, and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
  Lithium Ion Polymer Battery 3.7v 2500mAh: Lithium ion polymer (also known as 'lipo' or 'lipoly') batteries are thin, light and powerful. The output ranges from 4.2V when completely charged to 3.7V. This battery has a capacity of 2500mAh for a total of about 10 Wh. The batteries come pre-attached with a genuine 2-pin JST-PH connector as shown and include the necessary protection circuitry.
  Waterproof Pushbutton (white): Waterproof Illuminated Pushbutton (white)
